# Fritzing sketch sensorsSketch (saved by Fritzing 0.9.2b)
circuit board: 8.46667cm x 5.64444cm
breadboards: 1

parts:
  Part1 = Arduino Nano (Rev3.0)
  Part2 = Barometric Pressure Sensor - BMP180 Breakout (GY-68)
  DHT1 = DHT22 Humidity and Temperature Sensor
  Part4 = NRF24L01+ Breakout Board
  Part5 = BH1750
  Raspberry_Pi1 = Raspberry Pi 2
  Part6 = NRF24L01+ Breakout Board

nets:
  GND: Part1.GND, Part2.GND, DHT1.GND, Part4.GND, Part5.GND
  N1: Part1.D6, DHT1.DATA
  N2: Part1.D9, Part4.CE
  N3: Part1.D10, Part4.CS
  N4: Part1.D11/MOSI, Part4.MOSI
  N5: Part1.D12/MISO, Part4.MISO
  5V: Part1.5V, DHT1.VDD
  N6: Part1.A5, Part2.SCL, Part5.SCL
  N7: Part1.A4, Part2.SDA, Part5.SDA, Part5.ADDR
  VCC: Part1.3V3, Part2.VCC, Part4.VCC, Part5.VCC
  N8: Part1.D13/SCK, Part4.SCK
  3V3: Raspberry_Pi1.3v3, Part6.VCC
  N9: Raspberry_Pi1.GIPO22, Part6.CE
  N10: Raspberry_Pi1.GIPO10, Part6.MOSI
  N11: Raspberry_Pi1.GIPO9, Part6.MISO
  N12: Raspberry_Pi1.GIPO11, Part6.SCK
  N13: Raspberry_Pi1.GIPO8, Part6.CS
  GND_2: Raspberry_Pi1.GND, Part6.GND

custom parts:
  BH1750: Light Sensor
